# Fritzing sketch Rele temp e interruptor (saved by Fritzing 0.7.7b)
breadboards: 1

parts:
  Arduino1 = Arduino
  R1 = Resistor [tolerance=±5% resistance=1k package=THT]
  T1 = LM35 Temperature Sensor [package="TO92 [THT]"]
  D1 = Rectifier Diode [part_number=1N4001 package="300 mil [THT]"]
  Q1 = npn-Powertransistor [package="TO220 [THT]"]
  K1 = Relay [part_number=FRS1B-S package=THT]
  S1 = Square Pushbutton
  R2 = Resistor [tolerance=±5% resistance=10k package=THT]

nets:
  GND: Arduino1.GND, T1.GND, Q1.emitter, R2.Pin_0
  N1: Arduino1.D12, R1.Pin_1
  N2: Arduino1.D7, S1.leg0, R2.Pin_1
  N3: Arduino1.+5V, T1.+Vs, D1.cathode, K1.COIL2, K1.B, S1.leg1
  N4: Arduino1.A0, T1.Vout
  N5: R1.Pin_0, Q1.base
  N6: D1.anode, Q1.collector, K1.A, K1.COIL1
